# Fritzing sketch v4 (saved by Fritzing 0.9.3b)

parts:
  8-Channel_Relay1 = 8-Channel 5v Relay Shield [package=relay-8ch5v10a]
  J2 = Power Jack [package=power_jack_pth_lock]
  Componente7 = Arduino Nano (Rev3.0)
  Componente8 = NRF24L01+ Breakout Board
  KY-25 = Keyes Relay [package=THT]  # not connected
  KY-26 = Keyes Relay [package=THT]
  KY-27 = Keyes Relay [package=THT]
  ZS-042_RTC4 = ZS-042 RTC Module
  U5 = LM2596 step down module
  U6 = LM2596 step down module
  M16 = DC Motor
  M17 = DC Motor
  M18 = DC Motor
  M19 = DC Motor

nets:
  VCC: 8-Channel_Relay1.VCC, Componente7.VIN, KY-26.signal, KY-27.signal, U5.OUT+
  GND: 8-Channel_Relay1.GND, 8-Channel_Relay1.K1-In, 8-Channel_Relay1.K2-On, 8-Channel_Relay1.K3-In, 8-Channel_Relay1.K4-On, 8-Channel_Relay1.K5-In, 8-Channel_Relay1.K6-On, 8-Channel_Relay1.K7-In, 8-Channel_Relay1.K8-On, J2.GND, Componente7.GND, Componente8.GND, KY-26.power, KY-27.power, ZS-042_RTC4.GND, U5.IN-, U5.OUT-, U6.IN-, U6.OUT-
  N1: 8-Channel_Relay1.IN1, 8-Channel_Relay1.IN2, Componente7.D5
  N2: 8-Channel_Relay1.IN3, 8-Channel_Relay1.IN4, Componente7.D4
  N3: 8-Channel_Relay1.IN5, 8-Channel_Relay1.IN6, Componente7.D3
  N4: 8-Channel_Relay1.IN7, 8-Channel_Relay1.IN8, Componente7.D2
  N5: 8-Channel_Relay1.K1-Off, M16.pin_1
  N6: 8-Channel_Relay1.K1-On, 8-Channel_Relay1.K2-In, 8-Channel_Relay1.K3-On, 8-Channel_Relay1.K4-In, KY-27.C
  N7: 8-Channel_Relay1.K2-Off, M16.pin_2
  N8: 8-Channel_Relay1.K3-Off, M17.pin_1
  N9: 8-Channel_Relay1.K4-Off, M17.pin_2
  N10: 8-Channel_Relay1.K5-Off, M18.pin_1
  N11: 8-Channel_Relay1.K5-On, 8-Channel_Relay1.K6-In, 8-Channel_Relay1.K7-On, 8-Channel_Relay1.K8-In, KY-26.C
  N12: 8-Channel_Relay1.K6-Off, M18.pin_2
  N13: 8-Channel_Relay1.K7-Off, M19.pin_1
  N14: 8-Channel_Relay1.K8-Off, M19.pin_2
  N15: J2.PWR, U5.IN+, U6.IN+
  N16: Componente7.D7, Componente8.CE
  N17: Componente7.D8, Componente8.CS
  N18: Componente7.D9, KY-26.ground
  N19: Componente7.D10, KY-27.ground
  N20: Componente7.D11/MOSI, Componente8.MOSI
  N21: Componente7.D12/MISO, Componente8.MISO
  5V: Componente7.5V, ZS-042_RTC4.VCC
  N22: Componente7.A5, ZS-042_RTC4.SCL
  N23: Componente7.A4, ZS-042_RTC4.SDA
  3V3: Componente7.3V3, Componente8.VCC
  N24: Componente7.D13/SCK, Componente8.SCK
  N25: KY-26.NO, KY-27.NO, U6.OUT+

notes:
  V4
  V3
  V2
  V1
  + - S
  In: 12V
  Out: 5V
  In: 12V
  Out: 9V

custom parts:
  8-Channel 5v Relay Shield: 8 Channel 5v Relay Shield w. 2x SPD-06VDC-SD-C
  Keyes Relay: The Keyes 5V relay module is suitable for SCM development, home appliance control. It uses a 5V~12V TIL control signal which can control DC / AC signal.
  LM2596 step down module: LM2596 DC-DC step down power supply module 3 A.
